# Fritzing sketch pcb 1 (saved by Fritzing 0.9.3b)
circuit board: 6.5cm x 3.4cm
circuit board: 8.46667cm x 5.64444cm
breadboards: 1

parts:
  DRILL1 = MOSFET-NCHANNEL [package=to-92]
  DRILL2 = MOSFET-NCHANNEL [package=to-92]
  SD = MOSFET-NCHANNEL [package=to-92]
  LEGS = MOSFET-NCHANNEL [package=to-92]
  MicroSD = microSD Socket [package=usd-socket-pp]
  UV = female pin header, 2 pins [form="♀ (female)"]
  J2 = female pin header, 2 pins [form="♀ (female)"]
  Rm = Resistor [tolerance=±5% resistance=220 package=THT]
  Q1 = Basic FET P-Channel [package="D2Pak [SMD]"]  # not connected
  MOIST = female pin header, 1 pin [form="♀ (female)"]
  GND = female pin header, 1 pin [form="♀ (female)"]  # not connected
  J4 = female pin header, 1 pin [form="♀ (female)"]
  BMP = female pin header, 1 pin [form="♀ (female)"]
  PWR = female pin header, 1 pin [form="♀ (female)"]
  GPS = female pin header, 1 pin [form="♀ (female)"]
  J9 = female pin header, 1 pin [form="♀ (female)"]
  J10 = female pin header, 1 pin [form="♀ (female)"]
  XBEE = female pin header, 1 pin [form="♀ (female)"]
  J11 = female pin header, 1 pin [form="♀ (female)"]
  J12 = female pin header, 1 pin [form="♀ (female)"]
  PRO_Mini = Arduino Pro Mini v13
  MOSFET = female pin header, 1 pin [form="♀ (female)"]

nets:
  N1: DRILL1.D, MOSFET.pin1
  N2: DRILL1.G, PRO_Mini.D6_PWM
  N3: DRILL2.D, J11.pin1
  N4: DRILL2.G, PRO_Mini.D5_PWM
  N5: SD.D, MicroSD.SHIELD, MicroSD.GND
  N6: SD.G, PRO_Mini.D2
  N7: LEGS.D, J12.pin1
  N8: LEGS.G, PRO_Mini.D9_PWM
  N9: MicroSD.CS, PRO_Mini.D10_PWM/SS
  N10: MicroSD.DI, PRO_Mini.D11_PWM/MOSI
  VCC: MicroSD.VCC, UV.pin1, J2.pin2, PRO_Mini.VCC
  N11: MicroSD.SCK, PRO_Mini.D13/SCK
  N12: MicroSD.DO, PRO_Mini.D12/MISO
  N13: J2.pin1, PRO_Mini.A1
  N14: Rm.Pin_1, MOIST.pin1, PRO_Mini.A0
  N15: J4.pin1, PRO_Mini.A4
  N16: BMP.pin1, PRO_Mini.A5
  N17: PWR.pin1, PRO_Mini.RAW
  N18: GPS.pin1, PRO_Mini.D4
  N19: J9.pin1, PRO_Mini.D3_PWM
  N20: J10.pin1, PRO_Mini.D8
  N21: XBEE.pin1, PRO_Mini.D7

custom parts:
  Arduino Pro Mini v13: It's blue! It's thin! It's the Arduino Pro Mini! SparkFun's minimal design approach to Arduino. This is a 5V Arduino running the 16MHz bootloader. Arduino Pro Mini does not come with connectors populated so that you can solder in any connector or wire with any orientation you need. We recommend first time Arduino users start with the Uno R3. It's a great board that will get you up and running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
