# Fritzing sketch pcb 2 (saved by Fritzing 0.9.3b)
circuit board: 13.2007cm x 5.89078cm
circuit board: 6.5cm x 3.4cm
breadboards: 1

parts:
  BMP280 = Adafruit_BMP280
  XBEE = XBee
  U2 = Voltage Regulator LM1117 [package=sot223]
  solar = female pin header, 2 pins [form="♀ (female)"]  # not connected
  OUT = female pin header, 2 pins [form="♀ (female)"]
  BAT = female pin header, 2 pins [form="♀ (female)"]
  I2C = female pin header, 2 pins [form="♀ (female)"]
  XBEE_2 = female pin header, 2 pins [form="♀ (female)"]
  3_3V = female pin header, 1 pin [form="♀ (female)"]
  PWR = female pin header, 1 pin [form="♀ (female)"]
  GND = female pin header, 1 pin [form="♀ (female)"]  # not connected
  B = female pin header, 1 pin [form="♀ (female)"]
  GND1 = female pin header, 1 pin [form="♀ (female)"]  # not connected
  PWR1 = female pin header, 1 pin [form="♀ (female)"]
  Cin = Ceramic Capacitor [capacitance=100nF package="100 mil [THT, multilayer]"]
  COut = Ceramic Capacitor [capacitance=10µF package="100 mil [THT, multilayer]"]
  J1 = female pin header, 2 pins [form="♀ (female)"]
  J2 = female pin header, 1 pin [form="♀ (female)"]
  Q1 = MOSFET-NCHANNEL [package=sot23-3]
  R1 = Resistor [tolerance=±5% resistance=220 package="0805 [SMD]"]

nets:
  3.3V: BMP280.3.3V, XBEE.VCC, U2.OUT, 3_3V.pin1, COut.1
  GND: BMP280.GND
  N1: BMP280.SCK/SCL, I2C.pin2, J1.pin2
  N2: BMP280.SDI/SDA, I2C.pin1, J1.pin1
  N3: XBEE.pin2, XBEE_2.pin2
  N4: XBEE.pin3, XBEE_2.pin1
  N5: XBEE.pin20, Q1.G, R1.Pin_1
  N6: U2.IN, OUT.pin2, PWR.pin1, PWR1.pin1, Cin.1
  N7: BAT.pin1, B.pin1
  N8: J2.pin1, Q1.D
  N9: Q1.S, R1.Pin_0

custom parts:
  Adafruit_BMP280: Bosch has stepped up their game with their new BMP280 sensor, an environmental sensor with temperature, barometric pressure that is the next generation upgrade to the BMP085/BMP180/BMP183. This sensor is great for all sorts of weather sensing and can even be used in both I2C and SPI! This precision sensor from Bosch is the best low-cost, precision sensing solution for measuring barometric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
