# Fritzing sketch pcb1_DPAK (saved by Fritzing 0.9.3b)
circuit board: 8.46667cm x 5.64444cm
circuit board: 6.5cm x 3.4cm
breadboards: 1

parts:
  SD = MOSFET-NCHANNEL [package=to-92]
  MicroSD = microSD Socket [package=usd-socket-pp]
  UV = female pin header, 2 pins [form="♀ (female)"]
  J2 = female pin header, 2 pins [form="♀ (female)"]
  Rm = Resistor [tolerance=±5% resistance=220 package=THT]
  MOIST = female pin header, 1 pin [form="♀ (female)"]
  GND = female pin header, 1 pin [form="♀ (female)"]  # not connected
  J4 = female pin header, 1 pin [form="♀ (female)"]
  BMP = female pin header, 1 pin [form="♀ (female)"]
  PWR = female pin header, 1 pin [form="♀ (female)"]
  GPS = female pin header, 1 pin [form="♀ (female)"]
  J9 = female pin header, 1 pin [form="♀ (female)"]
  J10 = female pin header, 1 pin [form="♀ (female)"]
  XBEE = female pin header, 1 pin [form="♀ (female)"]
  J11 = female pin header, 1 pin [form="♀ (female)"]
  J12 = female pin header, 1 pin [form="♀ (female)"]
  PRO_Mini = Arduino Pro Mini v13
  MOSFET = female pin header, 1 pin [form="♀ (female)"]
  DRILL2 = MOSFET-NCHANNEL [package=dpak]
  DRILL1 = MOSFET-NCHANNEL [package=dpak]
  LEGS = MOSFET-NCHANNEL [package=dpak]

nets:
  N1: SD.D, MicroSD.SHIELD, MicroSD.GND
  N2: SD.G, PRO_Mini.D2
  N3: MicroSD.CS, PRO_Mini.D10_PWM/SS
  N4: MicroSD.DI, PRO_Mini.D11_PWM/MOSI
  VCC: MicroSD.VCC, UV.pin1, J2.pin2, PRO_Mini.VCC
  N5: MicroSD.SCK, PRO_Mini.D13/SCK
  N6: MicroSD.DO, PRO_Mini.D12/MISO
  N7: J2.pin1, PRO_Mini.A1
  N8: Rm.Pin_1, MOIST.pin1, PRO_Mini.A0
  N9: J4.pin1, PRO_Mini.A4
  N10: BMP.pin1, PRO_Mini.A5
  N11: PWR.pin1, PRO_Mini.RAW
  N12: GPS.pin1, PRO_Mini.D4
  N13: J9.pin1, PRO_Mini.D3_PWM
  N14: J10.pin1, PRO_Mini.D8
  N15: XBEE.pin1, PRO_Mini.D7
  N16: J11.pin1, DRILL1.D
  N17: J12.pin1, LEGS.D
  N18: PRO_Mini.D9_PWM, LEGS.G
  N19: PRO_Mini.D6_PWM, DRILL2.G
  N20: PRO_Mini.D5_PWM, DRILL1.G
  N21: MOSFET.pin1, DRILL2.D

custom parts:
  Arduino Pro Mini v13: It's blue! It's thin! It's the Arduino Pro Mini! SparkFun's minimal design approach to Arduino. This is a 5V Arduino running the 16MHz bootloader. Arduino Pro Mini does not come with connectors populated so that you can solder in any connector or wire with any orientation you need. We recommend first time Arduino users start with the Uno R3. It's a great board that will get you up and running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
