# Fritzing sketch pcb1_SOT23 (saved by Fritzing 0.9.3b)
circuit board: 8.46667cm x 5.64444cm
circuit board: 6.5cm x 3.4cm
breadboards: 1

parts:
  MicroSD = microSD Socket [package=usd-socket-pp]
  UV = female pin header, 2 pins [form="♀ (female)"]
  J2 = female pin header, 2 pins [form="♀ (female)"]
  Rm = Resistor [tolerance=±5% resistance=220 package=THT]
  MOIST = female pin header, 1 pin [form="♀ (female)"]
  GND = female pin header, 1 pin [form="♀ (female)"]  # not connected
  J4 = female pin header, 1 pin [form="♀ (female)"]
  I2C = female pin header, 1 pin [form="♀ (female)"]
  PWR = female pin header, 1 pin [form="♀ (female)"]
  GPS = female pin header, 1 pin [form="♀ (female)"]
  J9 = female pin header, 1 pin [form="♀ (female)"]
  J10 = female pin header, 1 pin [form="♀ (female)"]
  XBEE = female pin header, 1 pin [form="♀ (female)"]
  J11 = female pin header, 1 pin [form="♀ (female)"]
  J12 = female pin header, 1 pin [form="♀ (female)"]
  PRO_Mini = Arduino Pro Mini v13
  MFT = female pin header, 1 pin [form="♀ (female)"]
  L = MOSFET-NCHANNEL [package=sot23-3]
  D1 = MOSFET-NCHANNEL [package=sot23-3]
  D2 = MOSFET-NCHANNEL [package=sot23-3]
  R1 = Resistor [tolerance=±5% resistance=220 package="0805 [SMD]"]
  R2 = Resistor [tolerance=±5% resistance=220 package="0805 [SMD]"]
  R3 = Resistor [tolerance=±5% resistance=220 package="0805 [SMD]"]
  LD = female pin header, 1 pin [form="♀ (female)"]
  R4 = Resistor [tolerance=±5% resistance=220 package="0805 [SMD]"]

nets:
  N1: MicroSD.SHIELD, MicroSD.GND
  N2: MicroSD.CS, PRO_Mini.D10_PWM/SS
  N3: MicroSD.DI, PRO_Mini.D11_PWM/MOSI
  VCC: MicroSD.VCC, UV.pin1, J2.pin2, PRO_Mini.VCC, PRO_Mini.A3
  N4: MicroSD.SCK, PRO_Mini.D13/SCK
  N5: MicroSD.DO, PRO_Mini.D12/MISO
  N6: J2.pin1, PRO_Mini.A1
  N7: Rm.Pin_1, MOIST.pin1, PRO_Mini.A0
  N8: J4.pin1, PRO_Mini.A5
  N9: I2C.pin1, PRO_Mini.A4
  N10: PWR.pin1, PRO_Mini.RAW
  N11: GPS.pin1, PRO_Mini.D4
  N12: J9.pin1, PRO_Mini.D3_PWM
  N13: J10.pin1, PRO_Mini.D8
  N14: XBEE.pin1, PRO_Mini.D7
  N15: J11.pin1, L.D
  N16: J12.pin1, D2.D
  N17: PRO_Mini.D9_PWM, D1.G, R1.Pin_1
  N18: PRO_Mini.D6_PWM, D2.G, R2.Pin_1
  N19: PRO_Mini.D5_PWM, L.G, R3.Pin_1
  N20: PRO_Mini.D2, LD.pin1, R4.Pin_1
  N21: MFT.pin1, D1.D
  N22: L.S, R3.Pin_0
  N23: D1.S, R1.Pin_0
  N24: D2.S, R2.Pin_0

custom parts:
  Arduino Pro Mini v13: It's blue! It's thin! It's the Arduino Pro Mini! SparkFun's minimal design approach to Arduino. This is a 5V Arduino running the 16MHz bootloader. Arduino Pro Mini does not come with connectors populated so that you can solder in any connector or wire with any orientation you need. We recommend first time Arduino users start with the Uno R3. It's a great board that will get you up and running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
